# Fritzing sketch estacion_metereologica (saved by Fritzing 0.9.3b)
breadboards: 1

parts:
  Onderdeel2 = Arduino Uno (Rev3)
  LCD3 = LCD screen
  LCM1602_IIC3 = LCM1602 IIC [part_number="LCM1602 IIC" chip_label="LCM1602 IIC" package="DIP (Dual Inline) [THT]"]
  YL-83_-_Control_Board1 = YL-83 Rain Sensor - Control Board
  YL-83_-_Detection_Board1 = YL-83 Rain Sensor - Detection Board
  Part3 = FC-28 Soil Hygrometer Module - Probe
  Part4 = FC-28 Soil Hygrometer Module

nets:
  N1: Onderdeel2.A0, Part4.AO
  N2: Onderdeel2.A1, YL-83_-_Control_Board1.AO
  N3: Onderdeel2.D11_PWM/MOSI, Part4.DO
  N4: Onderdeel2.A4/SDA, LCM1602_IIC3.SDA
  N5: Onderdeel2.A5/SCL, LCM1602_IIC3.SCL
  VCC: Onderdeel2.5V, LCM1602_IIC3.VCC, YL-83_-_Control_Board1.VCC, Part4.VCC
  GND: Onderdeel2.GND, LCM1602_IIC3.GND, YL-83_-_Control_Board1.GND, Part4.GND
  VSS: LCD3.VSS, LCM1602_IIC3.VSS
  VDD: LCD3.VDD, LCM1602_IIC3.VDD
  N6: LCD3.V0, LCM1602_IIC3.V0
  N7: LCD3.RS, LCM1602_IIC3.RS
  N8: LCD3.R/W, LCM1602_IIC3.RW
  N9: LCD3.E, LCM1602_IIC3.E
  N10: LCD3.DB0, LCM1602_IIC3.D0
  N11: LCD3.DB1, LCM1602_IIC3.D1
  N12: LCD3.DB2, LCM1602_IIC3.D2
  N13: LCD3.DB3, LCM1602_IIC3.D3
  N14: LCD3.DB4, LCM1602_IIC3.D4
  N15: LCD3.DB5, LCM1602_IIC3.D5
  N16: LCD3.DB6, LCM1602_IIC3.D6
  N17: LCD3.DB7, LCM1602_IIC3.D7
  N18: LCD3.LED+, LCM1602_IIC3.A
  N19: LCD3.LED-, LCM1602_IIC3.K
  N20: LCM1602_IIC3.LED_A, LCM1602_IIC3.LED_B
  N21: YL-83_-_Control_Board1.POS, YL-83_-_Detection_Board1.POS
  N22: YL-83_-_Control_Board1.NEG, YL-83_-_Detection_Board1.NEG
  N23: Part3.POS, Part4.POS
  N24: Part3.NEG, Part4.NEG

custom parts:
  LCM1602 IIC: I2C-Module to use a 1602 or 2004 LCD on with the wire.h libory Serial LCD Modul
  YL-83 Rain Sensor - Control Board: The YL-83 is a rain sensor that has more resistance when dry and less resistance when wet. The module runs at 5V.
  YL-83 Rain Sensor - Detection Board: The YL-83 is a rain sensor that has more resistance when dry and less resistance when wet. The module runs at 5V.
  FC-28 Soil Hygrometer Module - Probe: The FC-28 is a soil hygrometer module that uses the Texas Instruments LM393 comparator chip to provide an analog measurement of soil humidity.
  FC-28 Soil Hygrometer Module: The FC-28 is a soil hygrometer module that uses the Texas Instruments LM393 comparator chip to provide an analog measurement of soil humidity. The digital output is high when soil moisture is over a certain threshold, as determined by adjusting the potentiometer.
